// Logisim project Final HERA Processor.circ as structural Verilog: 15 circuits, main circuit main
module main (
  input  in_1,
  input  Set_All,
  output [15:0] out_3,
  output [15:0] Current_Instruction
);

  wire alu_1_enable, alu_1_enable_2, and_1_out, and_2_out, and_3_out, branching_1_count, branching_1_load,
       button_1_out, call_return_1_enable_a, call_return_1_enable_b, call_return_1_enable_e,
       call_return_1_load_out, call_return_1_store_out, clock_1_out, not_1_out, not_2_out, not_3_out,
       or_2_out, or_3_out, or_7_out;
  wire [1:1] nor_1_out;
  wire [3:0] alu_1_output_2_register, call_return_1_select_e_to_r14, or_5_out, register_file_1_data_out_a,
       register_file_1_data_out_a_2, register_file_1_data_out_a_3, register_file_1_data_out_a_4,
       register_file_1_data_out_b, register_file_1_data_out_b_2, register_file_1_data_out_b_3,
       register_file_1_data_out_b_4, register_file_1_data_out_d_2, register_file_1_data_out_d_3;
  wire [4:0] alu_1_flags_out, flag_module_1_flags_out, multiplexer_1_out;
  wire [7:0] adder_1_out, register_file_1_data_out_d;
  wire [15:0] alu_1_output, alu_1_output_2, branching_1_data_out, call_return_1_pc_out,
       call_return_1_register_a_out, call_return_1_register_b_out, call_return_1_register_e_out, counter_1_q,
       demultiplexer_1_out1, or_1_out, or_6_out, ram_1_data, register_file_1_fp__register_14,
       register_file_1_register_1, register_file_1_register_2, register_file_1_register_3;

  assign or_1_out = branching_1_data_out | call_return_1_pc_out;  // OR_Gate or_1, 16 bits wide
  Branching branching_1 (
    .HERA_Instruction(Current_Instruction),
    .Register_B({register_file_1_data_out_b_4, register_file_1_data_out_b_3, register_file_1_data_out_b_2, register_file_1_data_out_b}),
    .Current_Instruction(counter_1_q), .Flags(flag_module_1_flags_out), .Load(branching_1_load),
    .Data_Out(branching_1_data_out), .Count(branching_1_count));
  Call_Return call_return_1 (
    .HERA_Instruction(Current_Instruction), .PC_In(counter_1_q),
    .Register_A_In({register_file_1_data_out_a_4, register_file_1_data_out_a_3, register_file_1_data_out_a_2, register_file_1_data_out_a}),
    .Register_B_In({register_file_1_data_out_b_4, register_file_1_data_out_b_3, register_file_1_data_out_b_2, register_file_1_data_out_b}),
    .FP__Register_14_In(register_file_1_fp__register_14), .PC_Out(call_return_1_pc_out),
    .Load_Out(call_return_1_load_out), .Store_Out(call_return_1_store_out),
    .Register_A_Out(call_return_1_register_a_out), .Enable_A(call_return_1_enable_a),
    .Register_B_Out(call_return_1_register_b_out), .Enable_B(call_return_1_enable_b),
    .Register_E_Out(call_return_1_register_e_out), .Enable_E(call_return_1_enable_e),
    .Select_E_to_R14(call_return_1_select_e_to_r14));
  or or_2 (or_2_out, branching_1_load, call_return_1_load_out);
  Counter #(.width(16), .max('hffff)) counter_1 (
    .load(or_2_out), .D(or_1_out), .count(and_1_out), .Q(counter_1_q), .clk(clock_1_out), .clr(in_1));  // open: carry
  Clock clock_1 (.out(clock_1_out));
  not not_1 (not_1_out, clock_1_out);
  and and_1 (and_1_out, branching_1_count, call_return_1_store_out);
  and and_2 (and_2_out, Current_Instruction[14], ~Current_Instruction[15], not_1_out);  // AND_Gate
  ROM #(.addrWidth(16), .dataWidth(16)) rom_1 (.addr(counter_1_q), .data(Current_Instruction));  // open: sel
  or or_3 (or_3_out, and_2_out, alu_1_enable);
  Demultiplexer #(.width(16), .disabled(0), .enable("false")) demultiplexer_1 (
    .out1(demultiplexer_1_out1), .in(ram_1_data), .sel(and_2_out));  // open: out0
  Adder adder_1 (
    .a({register_file_1_data_out_b_2, register_file_1_data_out_b}),
    .b({3'b000, Current_Instruction[12], Current_Instruction[7:4]}), .out(adder_1_out));  // open: cin, cout
  not not_2 (not_2_out, and_2_out);
  assign out_3 = demultiplexer_1_out1 | alu_1_output;  // OR_Gate or_4, 16 bits wide
  LED Carry_Block (.in(flag_module_1_flags_out[4]));
  LED Carry (.in(flag_module_1_flags_out[3]));
  Register_File register_file_1 (
    .Data_Out_A({register_file_1_data_out_a_4, register_file_1_data_out_a_3, register_file_1_data_out_a_2, register_file_1_data_out_a}),
    .Select_D(Current_Instruction[11:8]), .Select_A(Current_Instruction[7:4]), .Enable_D(or_3_out),
    .Data_Out_D({register_file_1_data_out_d_3, register_file_1_data_out_d_2, register_file_1_data_out_d}),
    .Register_1(register_file_1_register_1), .Register_2(register_file_1_register_2),
    .Register_3(register_file_1_register_3), .Clock(clock_1_out),
    .Data_Out_B({register_file_1_data_out_b_4, register_file_1_data_out_b_3, register_file_1_data_out_b_2, register_file_1_data_out_b}),
    .Select_B(Current_Instruction[3:0]), .Select_E(or_5_out), .Set_All(Set_All),
    .Enable_A(call_return_1_enable_a), .Enable_B(call_return_1_enable_b), .Enable_E(or_7_out),
    .Data_In_D(out_3), .Data_In_A(call_return_1_register_a_out), .Data_In_B(call_return_1_register_b_out),
    .Data_In_E(or_6_out), .FP__Register_14(register_file_1_fp__register_14));
  LED Overflow (.in(flag_module_1_flags_out[2]));
  LED Sign (.in(flag_module_1_flags_out[0]));
  LED Zero (.in(flag_module_1_flags_out[1]));
  RAM #(.dataWidth(16)) ram_1 (
    .addr(adder_1_out), .data(ram_1_data), .clk(and_2_out), .ld(not_3_out), .clr(button_1_out));  // open: sel
  not not_3 (not_3_out, Current_Instruction[13]);
  Button button_1 (.out(button_1_out));
  assign or_5_out = alu_1_output_2_register | call_return_1_select_e_to_r14;  // OR_Gate or_5, 4 bits wide
  assign or_6_out = alu_1_output_2 | call_return_1_register_e_out;  // OR_Gate or_6, 16 bits wide
  or or_7 (or_7_out, alu_1_enable_2, call_return_1_enable_e);
  assign ram_1_data = Current_Instruction[13] ? {register_file_1_data_out_d_3, register_file_1_data_out_d_2, register_file_1_data_out_d} : 16'bz;  // Controlled_Buffer control_buffer
  ALU alu_1 (
    .HERA_Instruction(Current_Instruction), .Flags_In(flag_module_1_flags_out),
    .Register_A({register_file_1_data_out_a_4, register_file_1_data_out_a_3, register_file_1_data_out_a_2, register_file_1_data_out_a}),
    .Register_B({register_file_1_data_out_b_4, register_file_1_data_out_b_3, register_file_1_data_out_b_2, register_file_1_data_out_b}),
    .Register_D({register_file_1_data_out_d_3, register_file_1_data_out_d_2, register_file_1_data_out_d}),
    .Enable(alu_1_enable), .Flags_Out(alu_1_flags_out), .Output(alu_1_output), .Output_2(alu_1_output_2),
    .Enable_2(alu_1_enable_2), .Output_2_Register(alu_1_output_2_register));
  Flag_Module flag_module_1 (.Flags_In(multiplexer_1_out), .clock(clock_1_out), .Flags_Out(flag_module_1_flags_out));
  and and_3 (and_3_out, ~Current_Instruction[13], not_2_out);  // AND_Gate
  Multiplexer #(.width(5), .enable("false")) multiplexer_1 (
    .in0(alu_1_flags_out), .in1({flag_module_1_flags_out[4:2], nor_1_out[1], ram_1_data[15]}),
    .out(multiplexer_1_out), .sel(and_3_out));
  Hex_Digit_Display hex_digit_display_1 (.value(register_file_1_register_1[15:12]));  // open: dp
  Hex_Digit_Display hex_digit_display_2 (.value(register_file_1_register_2[15:12]));  // open: dp
  Hex_Digit_Display hex_digit_display_3 (.value(register_file_1_register_3[15:12]));  // open: dp
  nor nor_1 (nor_1_out[1], ram_1_data[0], ram_1_data[1], ram_1_data[2], ram_1_data[3], ram_1_data[4], ram_1_data[5], ram_1_data[6], ram_1_data[7], ram_1_data[8], ram_1_data[9], ram_1_data[10], ram_1_data[11], ram_1_data[12], ram_1_data[13], ram_1_data[14], ram_1_data[15], ram_1_data[15]);
  Hex_Digit_Display hex_digit_display_4 (.value(register_file_1_register_1[11:8]));  // open: dp
  Hex_Digit_Display hex_digit_display_5 (.value(register_file_1_register_1[7:4]));  // open: dp
  Hex_Digit_Display hex_digit_display_6 (.value(register_file_1_register_2[11:8]));  // open: dp
  Hex_Digit_Display hex_digit_display_7 (.value(register_file_1_register_2[7:4]));  // open: dp
  Hex_Digit_Display hex_digit_display_8 (.value(register_file_1_register_3[11:8]));  // open: dp
  Hex_Digit_Display hex_digit_display_9 (.value(register_file_1_register_3[7:4]));  // open: dp
  Hex_Digit_Display hex_digit_display_10 (.value(register_file_1_register_1[3:0]));  // open: dp
  Hex_Digit_Display hex_digit_display_11 (.value(register_file_1_register_2[3:0]));  // open: dp
  Hex_Digit_Display hex_digit_display_12 (.value(register_file_1_register_3[3:0]));  // open: dp
  Hex_Digit_Display hex_digit_display_13 (.value(register_file_1_data_out_a_4));  // open: dp
  Hex_Digit_Display hex_digit_display_14 (.value(register_file_1_data_out_a_3));  // open: dp
  Hex_Digit_Display hex_digit_display_15 (.value(register_file_1_data_out_b_4));  // open: dp
  Hex_Digit_Display hex_digit_display_16 (.value(register_file_1_data_out_b_3));  // open: dp
  Hex_Digit_Display hex_digit_display_17 (.value(register_file_1_data_out_d_3));  // open: dp
  Hex_Digit_Display hex_digit_display_18 (.value(register_file_1_data_out_d_2));  // open: dp
  Joystick joystick_1 ();  // open: x, y
  Hex_Digit_Display hex_digit_display_19 (.value(register_file_1_data_out_a_2));  // open: dp
  Hex_Digit_Display hex_digit_display_20 (.value(register_file_1_data_out_a));  // open: dp
  Hex_Digit_Display hex_digit_display_21 (.value(register_file_1_data_out_b));  // open: dp
  Hex_Digit_Display hex_digit_display_22 (.value(register_file_1_data_out_b_2));  // open: dp
  Hex_Digit_Display hex_digit_display_23 (.value(register_file_1_data_out_d[3:0]));  // open: dp
  Hex_Digit_Display hex_digit_display_24 (.value(register_file_1_data_out_d[7:4]));  // open: dp
  Random random_1 ();  // open: clk, next, out, clr

  // Notes on the sheet:
  //   contents of rom_1 (hex, n*v repeats v):
  //   3160 e101 f100 e2ff f2ff a312 e102 f100 e2fb f2ff b321 b312 e102 f100 e2fe f2ff c321 e200 f200 c321
  //   e1ff f1ff 3180 e102 f100 31c0 e108 f100 3101 e102 f100 3111 e103 f100 e201 f200 6102 4302 e202 f200
  //   3068 b020 ed2f fd00 150d e205 f200
  //   Register 1
  //   Register 2
  //   Register 3
  //   Register A
  //   Register B
  //   Register D
endmodule

// Reg
module Register_File (
  input  [3:0] Select_E,
  input  [3:0] Select_D,
  input  Enable_A,
  input  Enable_B,
  input  Enable_D,
  input  Enable_E,
  input  [15:0] Data_In_A,
  input  [15:0] Data_In_B,
  input  [15:0] Data_In_D,
  input  [15:0] Data_In_E,
  input  [3:0] Select_A,
  input  Clock,
  input  Set_All,
  input  [3:0] Select_B,
  output [15:0] Data_Out_A,
  output [15:0] Data_Out_D,
  output [15:0] Register_1,
  output [15:0] Register_2,
  output [15:0] Register_3,
  output [15:0] FP__Register_14,
  output [15:0] Data_Out_B
);

  wire demultiplexer_1_out1, demultiplexer_1_out2, demultiplexer_1_out3, demultiplexer_1_out4,
       demultiplexer_1_out5, demultiplexer_1_out6, demultiplexer_1_out7, demultiplexer_1_out8,
       demultiplexer_1_out9, demultiplexer_1_out10, demultiplexer_1_out11, demultiplexer_1_out12,
       demultiplexer_1_out13, demultiplexer_1_out14, demultiplexer_1_out15, demultiplexer_2_out1,
       demultiplexer_2_out2, demultiplexer_2_out3, demultiplexer_2_out4, demultiplexer_2_out5,
       demultiplexer_2_out6, demultiplexer_2_out7, demultiplexer_2_out8, demultiplexer_2_out9,
       demultiplexer_2_out10, demultiplexer_2_out11, demultiplexer_2_out12, demultiplexer_2_out13,
       demultiplexer_2_out14, demultiplexer_2_out15, demultiplexer_3_out1, demultiplexer_3_out2,
       demultiplexer_3_out3, demultiplexer_3_out4, demultiplexer_3_out5, demultiplexer_3_out6,
       demultiplexer_3_out7, demultiplexer_3_out8, demultiplexer_3_out9, demultiplexer_3_out10,
       demultiplexer_3_out11, demultiplexer_3_out12, demultiplexer_3_out13, demultiplexer_3_out14,
       demultiplexer_3_out15, demultiplexer_4_out1, demultiplexer_4_out2, demultiplexer_4_out3,
       demultiplexer_4_out4, demultiplexer_4_out5, demultiplexer_4_out6, demultiplexer_4_out7,
       demultiplexer_4_out8, demultiplexer_4_out9, demultiplexer_4_out10, demultiplexer_4_out11,
       demultiplexer_4_out12, demultiplexer_4_out13, demultiplexer_4_out14, demultiplexer_4_out15, or_1_out,
       or_2_out, or_3_out, or_4_out, or_5_out, or_6_out, or_7_out, or_8_out, or_9_out, or_10_out, or_11_out,
       or_12_out, or_13_out, or_14_out, or_15_out;
  wire [15:0] demultiplexer_5_out1, demultiplexer_5_out2, demultiplexer_5_out3, demultiplexer_5_out4,
       demultiplexer_5_out5, demultiplexer_5_out6, demultiplexer_5_out7, demultiplexer_5_out8,
       demultiplexer_5_out9, demultiplexer_5_out10, demultiplexer_5_out11, demultiplexer_5_out12,
       demultiplexer_5_out13, demultiplexer_5_out14, demultiplexer_5_out15, demultiplexer_6_out1,
       demultiplexer_6_out2, demultiplexer_6_out3, demultiplexer_6_out4, demultiplexer_6_out5,
       demultiplexer_6_out6, demultiplexer_6_out7, demultiplexer_6_out8, demultiplexer_6_out9,
       demultiplexer_6_out10, demultiplexer_6_out11, demultiplexer_6_out12, demultiplexer_6_out13,
       demultiplexer_6_out14, demultiplexer_6_out15, demultiplexer_7_out1, demultiplexer_7_out2,
       demultiplexer_7_out3, demultiplexer_7_out4, demultiplexer_7_out5, demultiplexer_7_out6,
       demultiplexer_7_out7, demultiplexer_7_out8, demultiplexer_7_out9, demultiplexer_7_out10,
       demultiplexer_7_out11, demultiplexer_7_out12, demultiplexer_7_out13, demultiplexer_7_out14,
       demultiplexer_7_out15, demultiplexer_8_out1, demultiplexer_8_out2, demultiplexer_8_out3,
       demultiplexer_8_out4, demultiplexer_8_out5, demultiplexer_8_out6, demultiplexer_8_out7,
       demultiplexer_8_out8, demultiplexer_8_out9, demultiplexer_8_out10, demultiplexer_8_out11,
       demultiplexer_8_out12, demultiplexer_8_out13, demultiplexer_8_out14, demultiplexer_8_out15, or_16_out,
       or_17_out, or_18_out, or_19_out, or_20_out, or_21_out, or_22_out, or_23_out, or_24_out, or_25_out,
       or_26_out, or_27_out, or_28_out, or_29_out, or_30_out, register_1_q, register_5_q, register_6_q,
       register_7_q, register_8_q, register_9_q, register_10_q, register_11_q, register_12_q, register_13_q,
       register_14_q, register_16_q;

  Demultiplexer #(.select(4), .disabled(0), .enable("false")) demultiplexer_1 (
    .out1(demultiplexer_1_out1), .out2(demultiplexer_1_out2), .out3(demultiplexer_1_out3),
    .out4(demultiplexer_1_out4), .out5(demultiplexer_1_out5), .out6(demultiplexer_1_out6),
    .out7(demultiplexer_1_out7), .out8(demultiplexer_1_out8), .out9(demultiplexer_1_out9),
    .out10(demultiplexer_1_out10), .out11(demultiplexer_1_out11), .out12(demultiplexer_1_out12),
    .out13(demultiplexer_1_out13), .out14(demultiplexer_1_out14), .out15(demultiplexer_1_out15),
    .in(Enable_A), .sel(Select_A));  // open: out0
  Demultiplexer #(.select(4), .disabled(0), .enable("false")) demultiplexer_2 (
    .out1(demultiplexer_2_out1), .out2(demultiplexer_2_out2), .out3(demultiplexer_2_out3),
    .out4(demultiplexer_2_out4), .out5(demultiplexer_2_out5), .out6(demultiplexer_2_out6),
    .out7(demultiplexer_2_out7), .out8(demultiplexer_2_out8), .out9(demultiplexer_2_out9),
    .out10(demultiplexer_2_out10), .out11(demultiplexer_2_out11), .out12(demultiplexer_2_out12),
    .out13(demultiplexer_2_out13), .out14(demultiplexer_2_out14), .out15(demultiplexer_2_out15),
    .in(Enable_B), .sel(Select_B));  // open: out0
  Demultiplexer #(.select(4), .disabled(0), .enable("false")) demultiplexer_3 (
    .out1(demultiplexer_3_out1), .out2(demultiplexer_3_out2), .out3(demultiplexer_3_out3),
    .out4(demultiplexer_3_out4), .out5(demultiplexer_3_out5), .out6(demultiplexer_3_out6),
    .out7(demultiplexer_3_out7), .out8(demultiplexer_3_out8), .out9(demultiplexer_3_out9),
    .out10(demultiplexer_3_out10), .out11(demultiplexer_3_out11), .out12(demultiplexer_3_out12),
    .out13(demultiplexer_3_out13), .out14(demultiplexer_3_out14), .out15(demultiplexer_3_out15),
    .in(Enable_D), .sel(Select_D));  // open: out0
  Demultiplexer #(.select(4), .disabled(0), .enable("false")) demultiplexer_4 (
    .out1(demultiplexer_4_out1), .out2(demultiplexer_4_out2), .out3(demultiplexer_4_out3),
    .out4(demultiplexer_4_out4), .out5(demultiplexer_4_out5), .out6(demultiplexer_4_out6),
    .out7(demultiplexer_4_out7), .out8(demultiplexer_4_out8), .out9(demultiplexer_4_out9),
    .out10(demultiplexer_4_out10), .out11(demultiplexer_4_out11), .out12(demultiplexer_4_out12),
    .out13(demultiplexer_4_out13), .out14(demultiplexer_4_out14), .out15(demultiplexer_4_out15),
    .in(Enable_E), .sel(Select_E));  // open: out0
  or or_1 (or_1_out, demultiplexer_4_out1, demultiplexer_3_out1, demultiplexer_2_out1, demultiplexer_1_out1, Set_All);
  or or_2 (or_2_out, demultiplexer_4_out2, demultiplexer_3_out2, demultiplexer_2_out2, demultiplexer_1_out2, Set_All);
  or or_3 (or_3_out, demultiplexer_4_out3, demultiplexer_3_out3, demultiplexer_2_out3, demultiplexer_1_out3, Set_All);
  or or_4 (or_4_out, demultiplexer_4_out4, demultiplexer_3_out4, demultiplexer_2_out4, demultiplexer_1_out4, Set_All);
  or or_5 (or_5_out, demultiplexer_4_out5, demultiplexer_3_out5, demultiplexer_2_out5, demultiplexer_1_out5, Set_All);
  or or_6 (or_6_out, demultiplexer_4_out6, demultiplexer_3_out6, demultiplexer_2_out6, demultiplexer_1_out6, Set_All);
  or or_7 (or_7_out, demultiplexer_4_out7, demultiplexer_3_out7, demultiplexer_2_out7, demultiplexer_1_out7, Set_All);
  or or_8 (or_8_out, demultiplexer_4_out8, demultiplexer_3_out8, demultiplexer_2_out8, demultiplexer_1_out8, Set_All);
  or or_9 (or_9_out, demultiplexer_4_out9, demultiplexer_3_out9, demultiplexer_2_out9, demultiplexer_1_out9, Set_All);
  or or_10 (or_10_out, demultiplexer_4_out10, demultiplexer_3_out10, demultiplexer_2_out10, demultiplexer_1_out10, Set_All);
  or or_11 (or_11_out, demultiplexer_4_out11, demultiplexer_3_out11, demultiplexer_2_out11, demultiplexer_1_out11, Set_All);
  or or_12 (or_12_out, demultiplexer_4_out12, demultiplexer_3_out12, demultiplexer_2_out12, demultiplexer_1_out12, Set_All);
  or or_13 (or_13_out, demultiplexer_4_out13, demultiplexer_3_out13, demultiplexer_2_out13, demultiplexer_1_out13, Set_All);
  or or_14 (or_14_out, demultiplexer_4_out14, demultiplexer_3_out14, demultiplexer_2_out14, demultiplexer_1_out14, Set_All);
  or or_15 (or_15_out, demultiplexer_4_out15, demultiplexer_3_out15, demultiplexer_2_out15, demultiplexer_1_out15, Set_All);
  Demultiplexer #(.select(4), .width(16), .disabled(0), .enable("false")) demultiplexer_5 (
    .out1(demultiplexer_5_out1), .out2(demultiplexer_5_out2), .out3(demultiplexer_5_out3),
    .out4(demultiplexer_5_out4), .out5(demultiplexer_5_out5), .out6(demultiplexer_5_out6),
    .out7(demultiplexer_5_out7), .out8(demultiplexer_5_out8), .out9(demultiplexer_5_out9),
    .out10(demultiplexer_5_out10), .out11(demultiplexer_5_out11), .out12(demultiplexer_5_out12),
    .out13(demultiplexer_5_out13), .out14(demultiplexer_5_out14), .out15(demultiplexer_5_out15),
    .in(Data_In_A), .sel(Select_A));  // open: out0
  Demultiplexer #(.select(4), .width(16), .disabled(0), .enable("false")) demultiplexer_6 (
    .out1(demultiplexer_6_out1), .out2(demultiplexer_6_out2), .out3(demultiplexer_6_out3),
    .out4(demultiplexer_6_out4), .out5(demultiplexer_6_out5), .out6(demultiplexer_6_out6),
    .out7(demultiplexer_6_out7), .out8(demultiplexer_6_out8), .out9(demultiplexer_6_out9),
    .out10(demultiplexer_6_out10), .out11(demultiplexer_6_out11), .out12(demultiplexer_6_out12),
    .out13(demultiplexer_6_out13), .out14(demultiplexer_6_out14), .out15(demultiplexer_6_out15),
    .in(Data_In_B), .sel(Select_B));  // open: out0
  Demultiplexer #(.select(4), .width(16), .disabled(0), .enable("false")) demultiplexer_7 (
    .out1(demultiplexer_7_out1), .out2(demultiplexer_7_out2), .out3(demultiplexer_7_out3),
    .out4(demultiplexer_7_out4), .out5(demultiplexer_7_out5), .out6(demultiplexer_7_out6),
    .out7(demultiplexer_7_out7), .out8(demultiplexer_7_out8), .out9(demultiplexer_7_out9),
    .out10(demultiplexer_7_out10), .out11(demultiplexer_7_out11), .out12(demultiplexer_7_out12),
    .out13(demultiplexer_7_out13), .out14(demultiplexer_7_out14), .out15(demultiplexer_7_out15),
    .in(Data_In_D), .sel(Select_D));  // open: out0
  Demultiplexer #(.select(4), .width(16), .disabled(0), .enable("false")) demultiplexer_8 (
    .out1(demultiplexer_8_out1), .out2(demultiplexer_8_out2), .out3(demultiplexer_8_out3),
    .out4(demultiplexer_8_out4), .out5(demultiplexer_8_out5), .out6(demultiplexer_8_out6),
    .out7(demultiplexer_8_out7), .out8(demultiplexer_8_out8), .out9(demultiplexer_8_out9),
    .out10(demultiplexer_8_out10), .out11(demultiplexer_8_out11), .out12(demultiplexer_8_out12),
    .out13(demultiplexer_8_out13), .out14(demultiplexer_8_out14), .out15(demultiplexer_8_out15),
    .in(Data_In_E), .sel(Select_E));  // open: out0
  assign or_16_out = demultiplexer_8_out1 | demultiplexer_7_out1 | demultiplexer_6_out1 | demultiplexer_5_out1;  // OR_Gate or_16, 16 bits wide
  assign or_17_out = demultiplexer_8_out2 | demultiplexer_7_out2 | demultiplexer_6_out2 | demultiplexer_5_out2;  // OR_Gate or_17, 16 bits wide
  assign or_18_out = demultiplexer_8_out3 | demultiplexer_7_out3 | demultiplexer_6_out3 | demultiplexer_5_out3;  // OR_Gate or_18, 16 bits wide
  assign or_19_out = demultiplexer_8_out4 | demultiplexer_7_out4 | demultiplexer_6_out4 | demultiplexer_5_out4;  // OR_Gate or_19, 16 bits wide
  assign or_20_out = demultiplexer_8_out5 | demultiplexer_7_out5 | demultiplexer_6_out5 | demultiplexer_5_out5;  // OR_Gate or_20, 16 bits wide
  assign or_21_out = demultiplexer_8_out6 | demultiplexer_7_out6 | demultiplexer_6_out6 | demultiplexer_5_out6;  // OR_Gate or_21, 16 bits wide
  assign or_22_out = demultiplexer_8_out7 | demultiplexer_7_out7 | demultiplexer_6_out7 | demultiplexer_5_out7;  // OR_Gate or_22, 16 bits wide
  assign or_23_out = demultiplexer_8_out8 | demultiplexer_7_out8 | demultiplexer_6_out8 | demultiplexer_5_out8;  // OR_Gate or_23, 16 bits wide
  assign or_24_out = demultiplexer_8_out9 | demultiplexer_7_out9 | demultiplexer_6_out9 | demultiplexer_5_out9;  // OR_Gate or_24, 16 bits wide
  assign or_25_out = demultiplexer_8_out10 | demultiplexer_7_out10 | demultiplexer_6_out10 | demultiplexer_5_out10;  // OR_Gate or_25, 16 bits wide
  assign or_26_out = demultiplexer_8_out11 | demultiplexer_7_out11 | demultiplexer_6_out11 | demultiplexer_5_out11;  // OR_Gate or_26, 16 bits wide
  assign or_27_out = demultiplexer_8_out12 | demultiplexer_7_out12 | demultiplexer_6_out12 | demultiplexer_5_out12;  // OR_Gate or_27, 16 bits wide
  assign or_28_out = demultiplexer_8_out13 | demultiplexer_7_out13 | demultiplexer_6_out13 | demultiplexer_5_out13;  // OR_Gate or_28, 16 bits wide
  assign or_29_out = demultiplexer_8_out14 | demultiplexer_7_out14 | demultiplexer_6_out14 | demultiplexer_5_out14;  // OR_Gate or_29, 16 bits wide
  assign or_30_out = demultiplexer_8_out15 | demultiplexer_7_out15 | demultiplexer_6_out15 | demultiplexer_5_out15;  // OR_Gate or_30, 16 bits wide
  Register #(.width(16)) u_register_1 (.Q(register_1_q), .clk(Clock));  // open: D, en, clr
  Register #(.width(16)) u_register_2 (.D(or_16_out), .en(or_1_out), .Q(Register_1), .clk(Clock));  // open: clr
  Register #(.width(16)) u_register_3 (.D(or_17_out), .en(or_2_out), .Q(Register_2), .clk(Clock));  // open: clr
  Register #(.width(16)) register_4 (.D(or_18_out), .en(or_3_out), .Q(Register_3), .clk(Clock));  // open: clr
  Register #(.width(16)) register_5 (.D(or_19_out), .en(or_4_out), .Q(register_5_q), .clk(Clock));  // open: clr
  Register #(.width(16)) register_6 (.D(or_20_out), .en(or_5_out), .Q(register_6_q), .clk(Clock));  // open: clr
  Register #(.width(16)) register_7 (.D(or_21_out), .en(or_6_out), .Q(register_7_q), .clk(Clock));  // open: clr
  Register #(.width(16)) register_8 (.D(or_22_out), .en(or_7_out), .Q(register_8_q), .clk(Clock));  // open: clr
  Register #(.width(16)) register_9 (.D(or_23_out), .en(or_8_out), .Q(register_9_q), .clk(Clock));  // open: clr
  Register #(.width(16)) register_10 (.D(or_24_out), .en(or_9_out), .Q(register_10_q), .clk(Clock));  // open: clr
  Register #(.width(16)) register_11 (.D(or_25_out), .en(or_10_out), .Q(register_11_q), .clk(Clock));  // open: clr
  Register #(.width(16)) register_12 (.D(or_26_out), .en(or_11_out), .Q(register_12_q), .clk(Clock));  // open: clr
  Register #(.width(16)) register_13 (.D(or_27_out), .en(or_12_out), .Q(register_13_q), .clk(Clock));  // open: clr
  Register #(.width(16)) register_14 (.D(or_28_out), .en(or_13_out), .Q(register_14_q), .clk(Clock));  // open: clr
  Register #(.width(16)) register_15 (.D(or_29_out), .en(or_14_out), .Q(FP__Register_14), .clk(Clock));  // open: clr
  Register #(.width(16)) register_16 (.D(or_30_out), .en(or_15_out), .Q(register_16_q), .clk(Clock));  // open: clr
  Multiplexer #(.select(4), .width(16)) multiplexer_1 (
    .in0(register_1_q), .in1(Register_1), .in2(Register_2), .in3(Register_3), .in4(register_5_q),
    .in5(register_6_q), .in6(register_7_q), .in7(register_8_q), .in8(register_9_q), .in9(register_10_q),
    .in10(register_11_q), .in11(register_12_q), .in12(register_13_q), .in13(register_14_q),
    .in14(FP__Register_14), .in15(register_16_q), .out(Data_Out_A), .sel(Select_A));  // open: en
  Multiplexer #(.select(4), .width(16)) multiplexer_2 (
    .in0(register_1_q), .in1(Register_1), .in2(Register_2), .in3(Register_3), .in4(register_5_q),
    .in5(register_6_q), .in6(register_7_q), .in7(register_8_q), .in8(register_9_q), .in9(register_10_q),
    .in10(register_11_q), .in11(register_12_q), .in12(register_13_q), .in13(register_14_q),
    .in14(FP__Register_14), .in15(register_16_q), .out(Data_Out_B), .sel(Select_B));  // open: en
  Multiplexer #(.select(4), .width(16)) multiplexer_3 (
    .in0(register_1_q), .in1(Register_1), .in2(Register_2), .in3(Register_3), .in4(register_5_q),
    .in5(register_6_q), .in6(register_7_q), .in7(register_8_q), .in8(register_9_q), .in9(register_10_q),
    .in10(register_11_q), .in11(register_12_q), .in12(register_13_q), .in13(register_14_q),
    .in14(FP__Register_14), .in15(register_16_q), .out(Data_Out_D), .sel(Select_D));  // open: en
endmodule

module ALU (
  input  [15:0] HERA_Instruction,
  input  [4:0] Flags_In,
  input  [15:0] Register_A,
  input  [15:0] Register_B,
  input  [15:0] Register_D,
  output Enable,
  output Enable_2,
  output [3:0] Output_2_Register,
  output [4:0] Flags_Out,
  output [15:0] Output,
  output [15:0] Output_2
);

  wire multiplexer_3_out;
  wire [4:0] gates_math_1_add_flags, gates_math_1_and_flags, gates_math_1_mult_flags, gates_math_1_or_flags,
       gates_math_1_sub_flags, gates_math_1_xor_flags, inc_dec_1_decrement_flags, inc_dec_1_increment_flags,
       lsl_lsr_1_lsl_flags, lsl_lsr_1_lsr_flags, multiplexer_1_out, savf_restf_1_flags_out,
       setf_clrf_1_new_flags;
  wire [15:0] gates_math_1_add_output, gates_math_1_and_output, gates_math_1_mult_output_high,
       gates_math_1_mult_output_low, gates_math_1_or_output, gates_math_1_sub_output,
       gates_math_1_xor_output, inc_dec_1_decrement_out, inc_dec_1_increment_out, lsl_lsr_1_lsl_output,
       lsl_lsr_1_lsr_output, multiplexer_2_out, savf_restf_1_output, setlo_sethi_1_sethi, setlo_sethi_1_setlo;

  SAVF_RESTF savf_restf_1 (
    .HERA_Input(HERA_Instruction), .Register_D(Register_D), .Flags(Flags_In), .Output(savf_restf_1_output),
    .Flags_Out(savf_restf_1_flags_out));
  SETF_CLRF setf_clrf_1 (.HERA_Instruction(HERA_Instruction), .Flags(Flags_In), .New_Flags(setf_clrf_1_new_flags));
  LSL_LSR lsl_lsr_1 (
    .Register_B(Register_B), .Flags(Flags_In), .LSL_Output(lsl_lsr_1_lsl_output),
    .LSL_Flags(lsl_lsr_1_lsl_flags), .LSR_Output(lsl_lsr_1_lsr_output), .LSR_Flags(lsl_lsr_1_lsr_flags));
  Inc_Dec inc_dec_1 (
    .Register_D(Register_D), .HERA_Instruction(HERA_Instruction), .Flags(Flags_In),
    .Increment_Out(inc_dec_1_increment_out), .Increment_Flags(inc_dec_1_increment_flags),
    .Decrement_Out(inc_dec_1_decrement_out), .Decrement_Flags(inc_dec_1_decrement_flags));
  Multiplexer #(.select(4), .width(5)) multiplexer_1 (
    .in0(lsl_lsr_1_lsl_flags), .in1(lsl_lsr_1_lsr_flags), .in2(Flags_In), .in3(Flags_In), .in4(Flags_In),
    .in5(Flags_In), .in6(setf_clrf_1_new_flags), .in7(savf_restf_1_flags_out),
    .in8(inc_dec_1_increment_flags), .in9(inc_dec_1_increment_flags), .in10(inc_dec_1_increment_flags),
    .in11(inc_dec_1_increment_flags), .in12(inc_dec_1_decrement_flags), .in13(inc_dec_1_decrement_flags),
    .in14(inc_dec_1_decrement_flags), .in15(inc_dec_1_decrement_flags), .out(multiplexer_1_out),
    .sel(HERA_Instruction[7:4]));  // open: en
  Gates_Math gates_math_1 (
    .Register_A(Register_A), .Register_B(Register_B), .Flags(Flags_In), .And_Output(gates_math_1_and_output),
    .And_Flags(gates_math_1_and_flags), .Add_Output(gates_math_1_add_output),
    .Add_Flags(gates_math_1_add_flags), .Sub_Output(gates_math_1_sub_output),
    .Sub_Flags(gates_math_1_sub_flags), .Or_Output(gates_math_1_or_output), .Or_Flags(gates_math_1_or_flags),
    .XOr_Output(gates_math_1_xor_output), .XOr_Flags(gates_math_1_xor_flags),
    .Mult_Output_Low(gates_math_1_mult_output_low), .Mult_Output_High(gates_math_1_mult_output_high),
    .Mult_Flags(gates_math_1_mult_flags));
  Multiplexer #(.select(4), .width(16)) multiplexer_2 (
    .in0(lsl_lsr_1_lsl_output), .in1(lsl_lsr_1_lsr_output), .in2({16{1'b0}}), .in3({16{1'b0}}),
    .in4({16{1'b0}}), .in5({16{1'b0}}), .in6({16{1'b0}}), .in7(savf_restf_1_output),
    .in8(inc_dec_1_increment_out), .in9(inc_dec_1_increment_out), .in10(inc_dec_1_increment_out),
    .in11(inc_dec_1_increment_out), .in12(inc_dec_1_decrement_out), .in13(inc_dec_1_decrement_out),
    .in14(inc_dec_1_decrement_out), .in15(inc_dec_1_decrement_out), .out(multiplexer_2_out),
    .sel(HERA_Instruction[7:4]));  // open: en
  SETLO_SETHI setlo_sethi_1 (
    .HERA_Instruction(HERA_Instruction), .Register_D(Register_D), .SETLO(setlo_sethi_1_setlo),
    .SETHI(setlo_sethi_1_sethi));
  Multiplexer #(.select(4)) multiplexer_3 (
    .in0(1'b1), .in1(1'b1), .in2(1'b0), .in3(1'b0), .in4(1'b0), .in5(1'b0), .in6(1'b0), .in7(1'b1),
    .in8(1'b1), .in9(1'b1), .in10(1'b1), .in11(1'b1), .in12(1'b1), .in13(1'b1), .in14(1'b1), .in15(1'b1),
    .out(multiplexer_3_out), .sel(HERA_Instruction[7:4]));  // open: en
  Multiplexer #(.select(4)) multiplexer_4 (
    .in0(1'b0), .in1(1'b0), .in2(1'b0), .in3(multiplexer_3_out), .in4(1'b0), .in5(1'b0), .in6(1'b0),
    .in7(1'b0), .in8(1'b1), .in9(1'b1), .in10(1'b1), .in11(1'b1), .in12(1'b1), .in13(1'b1), .in14(1'b1),
    .in15(1'b1), .out(Enable), .sel(HERA_Instruction[15:12]));  // open: en
  Multiplexer #(.select(4), .width(5)) multiplexer_5 (
    .in0(Flags_In), .in1(Flags_In), .in2(Flags_In), .in3(multiplexer_1_out), .in4(Flags_In), .in5(Flags_In),
    .in6(Flags_In), .in7(Flags_In), .in8(gates_math_1_and_flags), .in9(gates_math_1_or_flags),
    .in10(gates_math_1_add_flags), .in11(gates_math_1_sub_flags), .in12(gates_math_1_mult_flags),
    .in13(gates_math_1_xor_flags), .in14(Flags_In), .in15(Flags_In), .out(Flags_Out),
    .sel(HERA_Instruction[15:12]));  // open: en
  Multiplexer #(.select(4), .width(16)) multiplexer_6 (
    .in0({16{1'b0}}), .in1({16{1'b0}}), .in2({16{1'b0}}), .in3(multiplexer_2_out), .in4({16{1'b0}}),
    .in5({16{1'b0}}), .in6({16{1'b0}}), .in7({16{1'b0}}), .in8(gates_math_1_and_output),
    .in9(gates_math_1_or_output), .in10(gates_math_1_add_output), .in11(gates_math_1_sub_output),
    .in12(gates_math_1_mult_output_low), .in13(gates_math_1_xor_output), .in14(setlo_sethi_1_setlo),
    .in15(setlo_sethi_1_sethi), .out(Output), .sel(HERA_Instruction[15:12]));  // open: en
  Multiplexer #(.select(4), .width(16)) multiplexer_7 (
    .in0({16{1'b0}}), .in1({16{1'b0}}), .in2({16{1'b0}}), .in3({16{1'b0}}), .in4({16{1'b0}}),
    .in5({16{1'b0}}), .in6({16{1'b0}}), .in7({16{1'b0}}), .in8({16{1'b0}}), .in9({16{1'b0}}),
    .in10({16{1'b0}}), .in11({16{1'b0}}), .in12(gates_math_1_mult_output_high), .in13({16{1'b0}}),
    .in14({16{1'b0}}), .in15({16{1'b0}}), .out(Output_2), .sel(HERA_Instruction[15:12]));  // open: en
  Multiplexer #(.select(4)) multiplexer_8 (
    .in0(1'b0), .in1(1'b0), .in2(1'b0), .in3(1'b0), .in4(1'b0), .in5(1'b0), .in6(1'b0), .in7(1'b0),
    .in8(1'b0), .in9(1'b0), .in10(1'b0), .in11(1'b0), .in12(1'b1), .in13(1'b0), .in14(1'b0), .in15(1'b0),
    .out(Enable_2), .sel(HERA_Instruction[15:12]));  // open: en
  Multiplexer #(.select(4), .width(4)) multiplexer_9 (
    .in0(4'b0000), .in1(4'b0000), .in2(4'b0000), .in3(4'b0000), .in4(4'b0000), .in5(4'b0000), .in6(4'b0000),
    .in7(4'b0000), .in8(4'b0000), .in9(4'b0000), .in10(4'b0000), .in11(4'b0000), .in12(4'b1101),
    .in13(4'b0000), .in14(4'b0000), .in15(4'b0000), .out(Output_2_Register), .sel(HERA_Instruction[15:12]));  // open: en

  // Notes on the sheet:
  //   Unspecified Values
endmodule

// SET
module SETLO_SETHI (
  input  [15:0] HERA_Instruction,
  input  [15:0] Register_D,
  output [15:0] SETLO,
  output [15:0] SETHI
);


  assign SETHI = {HERA_Instruction[7:0], Register_D[7:0]};
  assign SETLO = {{9{HERA_Instruction[7]}}, HERA_Instruction[6:0]};
endmodule

// FLG
module SETF_CLRF (
  input  [15:0] HERA_Instruction,
  input  [4:0] Flags,
  output [4:0] New_Flags
);

  wire [4:0] and_1_out, or_1_out;

  assign or_1_out = {HERA_Instruction[8], HERA_Instruction[3:0]} | Flags;  // OR_Gate or_1, 5 bits wide
  assign and_1_out = Flags & ~{HERA_Instruction[8], HERA_Instruction[3:0]};  // AND_Gate and_1, 5 bits wide
  Multiplexer #(.width(5)) multiplexer_1 (
    .in0(or_1_out), .in1(and_1_out), .out(New_Flags), .sel(HERA_Instruction[11]));  // open: en

  // Notes on the sheet:
  //   SETF/CLRF
  //   SET
  //   CLR
endmodule

// SHFT
module LSL_LSR (
  input  [15:0] Register_B,
  input  [4:0] Flags,
  output [15:0] LSL_Output,
  output [4:0] LSL_Flags,
  output [15:0] LSR_Output,
  output [4:0] LSR_Flags
);

  and and_1 (LSL_Output[0], Flags[3], ~Flags[4]);  // AND_Gate

  assign LSL_Flags = {Flags[4], Register_B[15], Flags[2:0]};
  assign LSL_Output[15:1] = Register_B[14:0];
  assign LSR_Flags = {Flags[4], Register_B[0], Flags[2:0]};
  assign LSR_Output = {LSL_Output[0], Register_B[15:1]};
endmodule

// Logic
module Gates_Math (
  input  [15:0] Register_A,
  input  [15:0] Register_B,
  input  [4:0] Flags,
  output [15:0] And_Output,
  output [4:0] And_Flags,
  output [15:0] Add_Output,
  output [4:0] Add_Flags,
  output [15:0] Sub_Output,
  output [4:0] Sub_Flags,
  output [15:0] Or_Output,
  output [4:0] Or_Flags,
  output [15:0] XOr_Output,
  output [4:0] XOr_Flags,
  output [15:0] Mult_Output_Low,
  output [15:0] Mult_Output_High,
  output [4:0] Mult_Flags
);

  wire and_1_out, and_3_out, nor_5_out, xor_1_out;
  wire [15:0] multiplexer_1_out, multiplexer_2_out, n16_bit_2_s_complement_1_output, negator_1_out,
       negator_2_out;
  wire [31:0] multiplier_1_out, negator_3_out;

  Multiplexer #(.width(16), .enable("false")) multiplexer_1 (
    .in0(Register_B), .in1(negator_2_out), .out(multiplexer_1_out), .sel(Register_B[15]));
  xor xor_1 (xor_1_out, Register_B[15], Register_A[15]);
  Negator #(.width(16)) negator_1 (.in(Register_A), .out(negator_1_out));
  Negator #(.width(16)) negator_2 (.in(Register_B), .out(negator_2_out));
  Multiplexer #(.width(16), .enable("false")) multiplexer_2 (
    .in0(Register_A), .in1(negator_1_out), .out(multiplexer_2_out), .sel(Register_A[15]));
  Multiplexer #(.width(32), .enable("false")) multiplexer_3 (
    .in0(multiplier_1_out), .in1(negator_3_out),
    .out({Mult_Flags[0], Mult_Output_High[14:0], Mult_Output_Low}), .sel(xor_1_out));
  Multiplier #(.width(16)) multiplier_1 (
    .a(multiplexer_2_out), .b(multiplexer_1_out), .out(multiplier_1_out[15:0]), .cout(multiplier_1_out[31:16]));  // open: cin
  Negator #(.width(32)) negator_3 (.in(multiplier_1_out), .out(negator_3_out));
  and and_1 (and_1_out, Flags[3], ~Flags[4]);  // AND_Gate
  assign {And_Flags[0], And_Output[14:0]} = Register_A & Register_B;  // AND_Gate and_2, 16 bits wide
  _16_Bit_Adder Add (
    .Carry_In(and_1_out), .Zero_Out(Add_Flags[1]), .Output(Add_Output), .Carry_Out(Add_Flags[3]),
    .Sign_Out(Add_Flags[0]), .Register_A(Register_A), .Overflow_Out(Add_Flags[2]), .Register_B(Register_B));
  _16_Bit_2_s_Complement u_16_bit_2_s_complement_1 (
    .Input(Register_B), .Output(n16_bit_2_s_complement_1_output));  // open: Carry
  assign {Or_Flags[0], Or_Output[14:0]} = Register_A | Register_B;  // OR_Gate or_1, 16 bits wide
  assign {XOr_Flags[0], XOr_Output[14:0]} = Register_A ^ Register_B;  // XOR_Gate xor_2, 16 bits wide
  nor nor_1 (And_Flags[1], 1'b0, And_Flags[0], And_Output[14], And_Output[13], And_Output[12], And_Output[11], And_Output[10], And_Output[9], And_Output[8], And_Output[7], And_Output[6], And_Output[5], And_Output[4], And_Output[3], And_Output[2], And_Output[1], And_Output[0]);
  _16_Bit_Adder Subtract (
    .Carry_In(and_1_out), .Zero_Out(Sub_Flags[1]), .Output(Sub_Output), .Carry_Out(Sub_Flags[3]),
    .Sign_Out(Sub_Flags[0]), .Register_A(Register_A), .Overflow_Out(Sub_Flags[2]),
    .Register_B(n16_bit_2_s_complement_1_output));
  nor nor_2 (Or_Flags[1], 1'b0, Or_Flags[0], Or_Output[14], Or_Output[13], Or_Output[12], Or_Output[11], Or_Output[10], Or_Output[9], Or_Output[8], Or_Output[7], Or_Output[6], Or_Output[5], Or_Output[4], Or_Output[3], Or_Output[2], Or_Output[1], Or_Output[0]);
  nor nor_3 (XOr_Flags[1], 1'b0, XOr_Flags[0], XOr_Output[14], XOr_Output[13], XOr_Output[12], XOr_Output[11], XOr_Output[10], XOr_Output[9], XOr_Output[8], XOr_Output[7], XOr_Output[6], XOr_Output[5], XOr_Output[4], XOr_Output[3], XOr_Output[2], XOr_Output[1], XOr_Output[0]);
  nor nor_4 (Mult_Flags[1], Mult_Flags[0], Mult_Output_High[14], Mult_Output_High[13], Mult_Output_High[12], Mult_Output_High[11], Mult_Output_High[10], Mult_Output_High[9], Mult_Output_High[8], Mult_Output_High[7], Mult_Output_High[6], Mult_Output_High[5], Mult_Output_High[4], Mult_Output_High[3], Mult_Output_High[2], Mult_Output_High[1], Mult_Output_High[0], Mult_Output_Low[15], Mult_Output_Low[14], Mult_Output_Low[13], Mult_Output_Low[12], Mult_Output_Low[11], Mult_Output_Low[10], Mult_Output_Low[9], Mult_Output_Low[8], Mult_Output_Low[7], Mult_Output_Low[6], Mult_Output_Low[5], Mult_Output_Low[4], Mult_Output_Low[3], Mult_Output_Low[2], Mult_Output_Low[1], Mult_Output_Low[0]);
  nor nor_5 (nor_5_out, Mult_Output_High[0], Mult_Output_High[1], Mult_Output_High[2], Mult_Output_High[3], Mult_Output_High[4], Mult_Output_High[5], Mult_Output_High[6], Mult_Output_High[7], Mult_Output_High[8], Mult_Output_High[9], Mult_Output_High[10], Mult_Output_High[11], Mult_Output_High[12], Mult_Output_High[13], Mult_Output_High[14], Mult_Flags[0], Mult_Output_Low[15]);
  and and_3 (and_3_out, Mult_Output_High[0], Mult_Output_High[1], Mult_Output_High[2], Mult_Output_High[3], Mult_Output_High[4], Mult_Output_High[5], Mult_Output_High[6], Mult_Output_High[7], Mult_Output_High[9], Mult_Output_High[10], Mult_Output_High[11], Mult_Output_High[12], Mult_Output_High[13], Mult_Output_High[14], Mult_Flags[0], Mult_Output_Low[15]);
  nor nor_6 (Mult_Flags[2], nor_5_out, and_3_out);

  assign Add_Flags[4] = Flags[4];
  assign And_Flags[4:2] = Flags[4:2];
  assign And_Output[15] = And_Flags[0];
  assign Mult_Flags[4:3] = Flags[4:3];
  assign Mult_Output_High[15] = Mult_Flags[0];
  assign Or_Flags[4:2] = Flags[4:2];
  assign Or_Output[15] = Or_Flags[0];
  assign Sub_Flags[4] = Flags[4];
  assign XOr_Flags[4:2] = Flags[4:2];
  assign XOr_Output[15] = XOr_Flags[0];
endmodule

// 2s C
module _16_Bit_2_s_Complement (
  input  [15:0] Input,
  output [15:0] Output,
  output Carry
);

  wire full_adder_1_carry_out, full_adder_2_carry_out, full_adder_3_carry_out, full_adder_4_carry_out,
       full_adder_5_carry_out, full_adder_6_carry_out, full_adder_7_carry_out, full_adder_8_carry_out,
       full_adder_9_carry_out, full_adder_10_carry_out, full_adder_11_carry_out, full_adder_12_carry_out,
       full_adder_13_carry_out, full_adder_14_carry_out, full_adder_15_carry_out, xor_1_out, xor_2_out,
       xor_3_out, xor_4_out, xor_5_out, xor_6_out, xor_7_out, xor_8_out, xor_9_out, xor_10_out, xor_11_out,
       xor_12_out, xor_13_out, xor_14_out, xor_15_out, xor_16_out;

  xor xor_1 (xor_1_out, Input[0], 1'b1);
  xor xor_2 (xor_2_out, Input[1], 1'b1);
  xor xor_3 (xor_3_out, Input[2], 1'b1);
  xor xor_4 (xor_4_out, Input[3], 1'b1);
  xor xor_5 (xor_5_out, Input[4], 1'b1);
  xor xor_6 (xor_6_out, Input[5], 1'b1);
  xor xor_7 (xor_7_out, Input[6], 1'b1);
  xor xor_8 (xor_8_out, Input[7], 1'b1);
  xor xor_9 (xor_9_out, Input[8], 1'b1);
  xor xor_10 (xor_10_out, Input[9], 1'b1);
  xor xor_11 (xor_11_out, Input[10], 1'b1);
  xor xor_12 (xor_12_out, Input[11], 1'b1);
  xor xor_13 (xor_13_out, Input[12], 1'b1);
  xor xor_14 (xor_14_out, Input[13], 1'b1);
  xor xor_15 (xor_15_out, Input[14], 1'b1);
  xor xor_16 (xor_16_out, Input[15], 1'b1);
  Full_Adder full_adder_1 (
    .Carry_In(1'b0), .Input_1(xor_1_out), .Input_2(1'b1), .Sum(Output[0]), .Carry_Out(full_adder_1_carry_out));
  Full_Adder full_adder_2 (
    .Carry_In(full_adder_15_carry_out), .Input_1(xor_9_out), .Input_2(1'b0), .Sum(Output[8]),
    .Carry_Out(full_adder_2_carry_out));
  Full_Adder full_adder_3 (
    .Carry_In(full_adder_1_carry_out), .Input_1(xor_2_out), .Input_2(1'b0), .Sum(Output[1]),
    .Carry_Out(full_adder_3_carry_out));
  Full_Adder full_adder_4 (
    .Carry_In(full_adder_2_carry_out), .Input_1(xor_10_out), .Input_2(1'b0), .Sum(Output[9]),
    .Carry_Out(full_adder_4_carry_out));
  Full_Adder full_adder_5 (
    .Carry_In(full_adder_3_carry_out), .Input_1(xor_3_out), .Input_2(1'b0), .Sum(Output[2]),
    .Carry_Out(full_adder_5_carry_out));
  Full_Adder full_adder_6 (
    .Carry_In(full_adder_5_carry_out), .Input_1(xor_4_out), .Input_2(1'b0), .Sum(Output[3]),
    .Carry_Out(full_adder_6_carry_out));
  Full_Adder full_adder_7 (
    .Carry_In(full_adder_4_carry_out), .Input_1(xor_11_out), .Input_2(1'b0), .Sum(Output[10]),
    .Carry_Out(full_adder_7_carry_out));
  Full_Adder full_adder_8 (
    .Carry_In(full_adder_7_carry_out), .Input_1(xor_12_out), .Input_2(1'b0), .Sum(Output[11]),
    .Carry_Out(full_adder_8_carry_out));
  Full_Adder full_adder_9 (
    .Carry_In(full_adder_6_carry_out), .Input_1(xor_5_out), .Input_2(1'b0), .Sum(Output[4]),
    .Carry_Out(full_adder_9_carry_out));
  Full_Adder full_adder_10 (
    .Carry_In(full_adder_8_carry_out), .Input_1(xor_13_out), .Input_2(1'b0), .Sum(Output[12]),
    .Carry_Out(full_adder_10_carry_out));
  Full_Adder full_adder_11 (
    .Carry_In(full_adder_9_carry_out), .Input_1(xor_6_out), .Input_2(1'b0), .Sum(Output[5]),
    .Carry_Out(full_adder_11_carry_out));
  Full_Adder full_adder_12 (
    .Carry_In(full_adder_10_carry_out), .Input_1(xor_14_out), .Input_2(1'b0), .Sum(Output[13]),
    .Carry_Out(full_adder_12_carry_out));
  Full_Adder full_adder_13 (
    .Carry_In(full_adder_11_carry_out), .Input_1(xor_7_out), .Input_2(1'b0), .Sum(Output[6]),
    .Carry_Out(full_adder_13_carry_out));
  Full_Adder full_adder_14 (
    .Carry_In(full_adder_12_carry_out), .Input_1(xor_15_out), .Input_2(1'b0), .Sum(Output[14]),
    .Carry_Out(full_adder_14_carry_out));
  Full_Adder full_adder_15 (
    .Carry_In(full_adder_13_carry_out), .Input_1(xor_8_out), .Input_2(1'b0), .Sum(Output[7]),
    .Carry_Out(full_adder_15_carry_out));
  Full_Adder full_adder_16 (
    .Carry_In(full_adder_14_carry_out), .Input_1(xor_16_out), .Input_2(1'b0), .Sum(Output[15]),
    .Carry_Out(Carry));
endmodule

// FA
module Full_Adder (
  input  Carry_In,
  input  Input_1,
  input  Input_2,
  output Sum,
  output Carry_Out
);

  wire and_1_out, and_2_out, xor_1_out;

  xor xor_1 (xor_1_out, Input_1, Input_2);
  and and_1 (and_1_out, Input_1, Input_2);
  xor xor_2 (Sum, Carry_In, xor_1_out);
  and and_2 (and_2_out, Carry_In, xor_1_out);
  or or_1 (Carry_Out, and_2_out, and_1_out);
endmodule

// Adder
module _16_Bit_Adder (
  input  [15:0] Register_A,
  input  Carry_In,
  input  [15:0] Register_B,
  output Zero_Out,
  output Overflow_Out,
  output [15:0] Output,
  output Carry_Out,
  output Sign_Out
);

  wire and_1_out, and_2_out, full_adder_1_carry_out, full_adder_2_carry_out, full_adder_3_carry_out,
       full_adder_4_carry_out, full_adder_5_carry_out, full_adder_6_carry_out, full_adder_7_carry_out,
       full_adder_8_carry_out, full_adder_9_carry_out, full_adder_10_carry_out, full_adder_11_carry_out,
       full_adder_12_carry_out, full_adder_13_carry_out, full_adder_14_carry_out, full_adder_15_carry_out;

  Full_Adder full_adder_1 (
    .Carry_In(Carry_In), .Input_1(Register_A[0]), .Input_2(Register_B[0]), .Sum(Output[0]),
    .Carry_Out(full_adder_1_carry_out));
  Full_Adder full_adder_2 (
    .Carry_In(full_adder_1_carry_out), .Input_1(Register_A[1]), .Input_2(Register_B[1]), .Sum(Output[1]),
    .Carry_Out(full_adder_2_carry_out));
  Full_Adder full_adder_3 (
    .Carry_In(full_adder_2_carry_out), .Input_1(Register_A[2]), .Input_2(Register_B[2]), .Sum(Output[2]),
    .Carry_Out(full_adder_3_carry_out));
  Full_Adder full_adder_4 (
    .Carry_In(full_adder_3_carry_out), .Input_1(Register_A[3]), .Input_2(Register_B[3]), .Sum(Output[3]),
    .Carry_Out(full_adder_4_carry_out));
  Full_Adder full_adder_5 (
    .Carry_In(full_adder_4_carry_out), .Input_1(Register_A[4]), .Input_2(Register_B[4]), .Sum(Output[4]),
    .Carry_Out(full_adder_5_carry_out));
  Full_Adder full_adder_6 (
    .Carry_In(full_adder_5_carry_out), .Input_1(Register_A[5]), .Input_2(Register_B[5]), .Sum(Output[5]),
    .Carry_Out(full_adder_6_carry_out));
  Full_Adder full_adder_7 (
    .Carry_In(full_adder_6_carry_out), .Input_1(Register_A[6]), .Input_2(Register_B[6]), .Sum(Output[6]),
    .Carry_Out(full_adder_7_carry_out));
  Full_Adder full_adder_8 (
    .Carry_In(full_adder_7_carry_out), .Input_1(Register_A[7]), .Input_2(Register_B[7]), .Sum(Output[7]),
    .Carry_Out(full_adder_8_carry_out));
  Full_Adder full_adder_9 (
    .Carry_In(full_adder_8_carry_out), .Input_1(Register_A[8]), .Input_2(Register_B[8]), .Sum(Output[8]),
    .Carry_Out(full_adder_9_carry_out));
  Full_Adder full_adder_10 (
    .Carry_In(full_adder_9_carry_out), .Input_1(Register_A[9]), .Input_2(Register_B[9]), .Sum(Output[9]),
    .Carry_Out(full_adder_10_carry_out));
  Full_Adder full_adder_11 (
    .Carry_In(full_adder_10_carry_out), .Input_1(Register_A[10]), .Input_2(Register_B[10]), .Sum(Output[10]),
    .Carry_Out(full_adder_11_carry_out));
  Full_Adder full_adder_12 (
    .Carry_In(full_adder_11_carry_out), .Input_1(Register_A[11]), .Input_2(Register_B[11]), .Sum(Output[11]),
    .Carry_Out(full_adder_12_carry_out));
  Full_Adder full_adder_13 (
    .Carry_In(full_adder_12_carry_out), .Input_1(Register_A[12]), .Input_2(Register_B[12]), .Sum(Output[12]),
    .Carry_Out(full_adder_13_carry_out));
  nor nor_1 (Zero_Out, Output[0], Output[1], Output[2], Output[3], Output[4], Output[5], Output[6], Output[7], Output[8], Output[9], Output[10], Output[11], Output[12], Output[13], Output[14], Output[15]);
  Full_Adder full_adder_14 (
    .Carry_In(full_adder_13_carry_out), .Input_1(Register_A[13]), .Input_2(Register_B[13]), .Sum(Output[13]),
    .Carry_Out(full_adder_14_carry_out));
  Full_Adder full_adder_15 (
    .Carry_In(full_adder_14_carry_out), .Input_1(Register_A[14]), .Input_2(Register_B[14]), .Sum(Output[14]),
    .Carry_Out(full_adder_15_carry_out));
  Full_Adder full_adder_16 (
    .Carry_In(full_adder_15_carry_out), .Input_1(Register_A[15]), .Input_2(Register_B[15]), .Sum(Output[15]),
    .Carry_Out(Carry_Out));
  or or_1 (Overflow_Out, and_1_out, and_2_out);
  and and_1 (and_1_out, ~Register_A[15], ~Register_B[15], Output[15]);  // AND_Gate
  and and_2 (and_2_out, Register_A[15], Register_B[15], ~Output[15]);  // AND_Gate

  assign Sign_Out = Output[15];
endmodule

// Flg
module Flag_Module (
  input  [4:0] Flags_In,
  input  clock,
  output [4:0] Flags_Out
);

  D_Flip_Flop Cary_Block (.clk(clock), .D(Flags_In[4]), .Q(Flags_Out[4]));  // open: Qn, preset, en, reset
  D_Flip_Flop Cary (.clk(clock), .D(Flags_In[3]), .Q(Flags_Out[3]));  // open: Qn, preset, en, reset
  D_Flip_Flop Overflow (.clk(clock), .D(Flags_In[2]), .Q(Flags_Out[2]));  // open: Qn, preset, en, reset
  D_Flip_Flop Zero (.clk(clock), .D(Flags_In[1]), .Q(Flags_Out[1]));  // open: Qn, preset, en, reset
  D_Flip_Flop Sign (.clk(clock), .D(Flags_In[0]), .Q(Flags_Out[0]));  // open: Qn, preset, en, reset
endmodule

module Inc_Dec (
  input  [15:0] Register_D,
  input  [15:0] HERA_Instruction,
  input  [4:0] Flags,
  output [15:0] Increment_Out,
  output [4:0] Increment_Flags,
  output [15:0] Decrement_Out,
  output [4:0] Decrement_Flags
);

  wire [15:0] n16_bit_2_s_complement_1_output, n16_bit_adder_1_output;

  _16_Bit_Adder u_16_bit_adder_1 (
    .Carry_In(1'b1), .Output(n16_bit_adder_1_output), .Register_A({{10{1'b0}}, HERA_Instruction[5:0]}),
    .Register_B({16{1'b0}}));  // open: Zero_Out, Carry_Out, Sign_Out, Overflow_Out
  _16_Bit_2_s_Complement u_16_bit_2_s_complement_1 (
    .Input(n16_bit_adder_1_output), .Output(n16_bit_2_s_complement_1_output));  // open: Carry
  _16_Bit_Adder u_16_bit_adder_2 (
    .Carry_In(1'b0), .Zero_Out(Increment_Flags[1]), .Output(Increment_Out), .Carry_Out(Increment_Flags[3]),
    .Sign_Out(Increment_Flags[0]), .Register_A(Register_D), .Overflow_Out(Increment_Flags[2]),
    .Register_B(n16_bit_adder_1_output));
  _16_Bit_Adder u_16_bit_adder_3 (
    .Carry_In(1'b0), .Zero_Out(Decrement_Flags[1]), .Output(Decrement_Out), .Carry_Out(Decrement_Flags[3]),
    .Sign_Out(Decrement_Flags[0]), .Register_A(Register_D), .Overflow_Out(Decrement_Flags[2]),
    .Register_B(n16_bit_2_s_complement_1_output));

  assign Decrement_Flags[4] = Flags[4];
  assign Increment_Flags[4] = Flags[4];
endmodule

// SAVF
module SAVF_RESTF (
  input  [15:0] HERA_Input,
  input  [15:0] Register_D,
  input  [4:0] Flags,
  output [15:0] Output,
  output [4:0] Flags_Out
);

  Multiplexer #(.width(16), .enable("false")) multiplexer_1 (
    .in0({{11{1'b0}}, Flags}), .in1(Register_D), .out(Output), .sel(HERA_Input[3]));
  Multiplexer #(.width(5), .enable("false")) multiplexer_2 (
    .in0(Flags), .in1(Register_D[4:0]), .out(Flags_Out), .sel(HERA_Input[3]));
endmodule

// BR
module Branching (
  input  [15:0] HERA_Instruction,
  input  [15:0] Register_B,
  input  [15:0] Current_Instruction,
  input  [4:0] Flags,
  output Load,
  output [15:0] Data_Out,
  output Count
);

  wire multiplexer_3_out, not_1_out, not_2_out, not_3_out, not_4_out, not_5_out, not_6_out, not_7_out,
       not_8_out, or_1_out, or_2_out, or_3_out, or_4_out, xor_1_out;
  wire [15:0] adder_1_out, adder_2_out, multiplexer_1_out, multiplexer_2_out;

  Adder #(.width(16)) adder_1 (.a(Current_Instruction), .b(16'h1), .out(adder_1_out));  // open: cin, cout
  xor xor_1 (xor_1_out, Flags[0], Flags[2]);
  Multiplexer #(.width(16), .enable("false")) multiplexer_1 (
    .in0(Register_B), .in1(adder_1_out), .out(multiplexer_1_out), .sel(or_1_out));
  or or_1 (or_1_out, HERA_Instruction[4], HERA_Instruction[5], HERA_Instruction[6], HERA_Instruction[7]);
  or or_2 (or_2_out, ~Flags[3], Flags[1]);  // OR_Gate
  Adder #(.width(16)) adder_2 (
    .a({{9{HERA_Instruction[7]}}, HERA_Instruction[6:0]}), .b(Current_Instruction), .out(adder_2_out));  // open: cin, cout
  Multiplexer #(.width(16), .enable("false")) multiplexer_2 (
    .in0(adder_2_out), .in1(multiplexer_1_out), .out(multiplexer_2_out), .sel(HERA_Instruction[12]));
  or or_3 (or_3_out, Flags[1], xor_1_out);
  not not_1 (not_1_out, xor_1_out);
  not not_2 (not_2_out, or_3_out);
  not not_3 (not_3_out, or_2_out);
  not not_4 (not_4_out, Flags[1]);
  not not_5 (not_5_out, Flags[3]);
  not not_6 (not_6_out, Flags[0]);
  not not_7 (not_7_out, Flags[2]);
  not not_8 (not_8_out, multiplexer_3_out);
  Multiplexer #(.select(4), .enable("false")) multiplexer_3 (
    .in0(1'b1), .in2(xor_1_out), .in3(not_1_out), .in4(or_3_out), .in5(not_2_out), .in6(or_2_out),
    .in7(not_3_out), .in8(Flags[1]), .in9(not_4_out), .in10(Flags[3]), .in11(not_5_out), .in12(Flags[0]),
    .in13(not_6_out), .in14(Flags[2]), .in15(not_7_out), .out(multiplexer_3_out), .sel(HERA_Instruction[11:8]));  // open: in1
  or or_4 (or_4_out, HERA_Instruction[13], HERA_Instruction[14], HERA_Instruction[15]);
  Multiplexer #(.enable("false")) multiplexer_4 (.in0(multiplexer_3_out), .in1(1'b0), .out(Load), .sel(or_4_out));
  Multiplexer #(.width(16), .enable("false")) multiplexer_5 (
    .in0(multiplexer_2_out), .in1({16{1'b0}}), .out(Data_Out), .sel(or_4_out));
  Multiplexer #(.enable("false")) multiplexer_6 (.in0(not_8_out), .in1(1'b1), .out(Count), .sel(or_4_out));
endmodule

module Call_Return (
  input  [15:0] HERA_Instruction,
  input  [15:0] PC_In,
  input  [15:0] Register_A_In,
  input  [15:0] Register_B_In,
  input  [15:0] FP__Register_14_In,
  output [15:0] PC_Out,
  output Load_Out,
  output Store_Out,
  output [15:0] Register_A_Out,
  output Enable_A,
  output [15:0] Register_B_Out,
  output Enable_B,
  output [15:0] Register_E_Out,
  output Enable_E,
  output [3:0] Select_E_to_R14
);

  wire nor_1_out;
  wire [15:0] adder_1_out, multiplexer_1_out;

  Adder #(.width(16)) adder_1 (.a(PC_In), .b(16'h1), .out(adder_1_out));  // open: cin, cout
  nor nor_1 (nor_1_out, HERA_Instruction[15], HERA_Instruction[14], ~HERA_Instruction[13], HERA_Instruction[12], HERA_Instruction[11], HERA_Instruction[10], HERA_Instruction[9]);  // NOR_Gate
  Multiplexer #(.width(16), .enable("false")) multiplexer_1 (
    .in0(adder_1_out), .in1(Register_B_In), .out(multiplexer_1_out), .sel(HERA_Instruction[8]));
  Multiplexer #(.width(16), .enable("false")) multiplexer_2 (
    .in0({16{1'b0}}), .in1(Register_B_In), .out(PC_Out), .sel(nor_1_out));
  Multiplexer #(.enable("false")) multiplexer_3 (.in0(1'b0), .in1(1'b1), .out(Load_Out), .sel(nor_1_out));
  Multiplexer #(.width(16), .enable("false")) multiplexer_4 (
    .in0({16{1'b0}}), .in1(FP__Register_14_In), .out(Register_A_Out), .sel(nor_1_out));
  Multiplexer #(.enable("false")) multiplexer_5 (.in0(1'b0), .in1(1'b1), .out(Enable_A), .sel(nor_1_out));
  Multiplexer #(.width(16), .enable("false")) multiplexer_6 (
    .in0({16{1'b0}}), .in1(multiplexer_1_out), .out(Register_B_Out), .sel(nor_1_out));
  Multiplexer #(.enable("false")) multiplexer_7 (.in0(1'b0), .in1(1'b1), .out(Enable_B), .sel(nor_1_out));
  Multiplexer #(.width(16), .enable("false")) multiplexer_8 (
    .in0({16{1'b0}}), .in1(Register_A_In), .out(Register_E_Out), .sel(nor_1_out));
  Multiplexer #(.enable("false")) multiplexer_9 (.in0(1'b0), .in1(1'b1), .out(Enable_E), .sel(nor_1_out));
  Multiplexer #(.width(4), .enable("false")) multiplexer_10 (
    .in0(4'b0000), .in1(4'b1110), .out(Select_E_to_R14), .sel(nor_1_out));
  not not_1 (Store_Out, Load_Out);
endmodule
